// Logisim project MiniMIPS.circ as structural Verilog: 4 circuits, main circuit MIPS32
module Decode (
  input  [31:0] in_1,
  output [5:0] out_2,
  output [31:0] out_3,
  output [4:0] out_4,
  output [4:0] out_5,
  output [4:0] out_6
);

  wire and_2_out, and_3_out, and_4_out, and_5_out, nor_1_out, not_1_out, not_9_out, not_10_out, or_1_out,
       or_2_out, or_3_out, or_4_out, xor_1_out;
  wire [4:4] not_6_out;
  wire [5:0] multiplexer_1_out, multiplexer_5_out, multiplexer_8_out, multiplexer_9_out, multiplexer_10_out,
       multiplexer_11_out;
  wire [5:4] not_2_out, not_3_out;
  wire [5:5] not_7_out, not_8_out;
  wire [31:0] bit_extender_1_out, bit_extender_2_out, bit_extender_3_out, multiplexer_2_out;

  and and_1 (not_2_out[5], in_1[31], in_1[30]);
  not not_1 (not_1_out, in_1[28]);
  nor nor_1 (nor_1_out, in_1[31], in_1[30], in_1[29], in_1[28], in_1[27], in_1[26]);
  and and_2 (and_2_out, in_1[29], not_1_out, in_1[27]);
  and and_3 (and_3_out, in_1[28], in_1[27], in_1[26]);
  or or_1 (or_1_out, and_2_out, and_3_out);
  not not_2 (not_2_out[4], not_2_out[5]);
  not not_3 (not_3_out[4], not_2_out[5]);
  not not_4 (not_3_out[5], not_2_out[5]);
  Multiplexer #(.width(6), .enable("false")) multiplexer_1 (
    .in0({not_2_out, in_1[28:26], not_2_out[5]}), .in1({not_3_out, in_1[28:27], not_2_out[5], in_1[26]}),
    .out(multiplexer_1_out), .sel(or_1_out));
  // NOT_Gate not_5 has open pins: in=nor_1_out, out=open
  assign bit_extender_1_out = {{27{1'b0}}, in_1[10:6]};  // Bit_Extender bit_extender_1
  assign bit_extender_2_out = {{16{in_1[15]}}, in_1[15:0]};  // Bit_Extender bit_extender_2
  assign bit_extender_3_out = {{16{1'b0}}, in_1[15:0]};  // Bit_Extender bit_extender_3
  not not_6 (not_6_out[4], not_2_out[5]);
  Multiplexer #(.width(32), .enable("false")) multiplexer_2 (
    .in0(bit_extender_2_out), .in1(bit_extender_3_out), .out(multiplexer_2_out), .sel(in_1[28]));
  Multiplexer #(.width(32), .enable("false")) multiplexer_3 (
    .in0(bit_extender_1_out), .in1(multiplexer_2_out), .out(out_3), .sel(in_1[29]));
  Multiplexer #(.width(5), .enable("false")) multiplexer_4 (
    .in0(in_1[15:11]), .in1(in_1[20:16]), .out(out_4), .sel(in_1[29]));
  Multiplexer #(.width(6), .enable("false")) multiplexer_5 (
    .in0({not_2_out[5], not_6_out[4], not_2_out[5], in_1[1], not_2_out[5], in_1[0]}),
    .in1({{3{not_2_out[5]}}, in_1[1], not_2_out[5], in_1[0]}), .out(multiplexer_5_out), .sel(in_1[2]));
  or or_2 (or_2_out, in_1[29], in_1[5]);
  Multiplexer #(.width(5), .enable("false")) multiplexer_6 (
    .in0(in_1[20:16]), .in1(in_1[25:21]), .out(out_5), .sel(or_2_out));
  not not_7 (not_7_out[5], not_2_out[5]);
  Multiplexer #(.width(5), .enable("false")) multiplexer_7 (
    .in0(in_1[25:21]), .in1(in_1[20:16]), .out(out_6), .sel(in_1[5]));
  Multiplexer #(.width(6), .enable("false")) multiplexer_8 (
    .in0({{2{not_2_out[5]}}, in_1[2:0], not_2_out[5]}),
    .in1({not_7_out[5], not_2_out[5], in_1[2:1], not_2_out[5], in_1[0]}), .out(multiplexer_8_out),
    .sel(in_1[3]));
  Multiplexer #(.width(6), .enable("false")) multiplexer_9 (
    .in0({in_1[0], not_2_out[5], in_1[3:2], not_2_out[5], in_1[1]}), .in1(multiplexer_8_out),
    .out(multiplexer_9_out), .sel(in_1[5]));
  or or_3 (or_3_out, in_1[3], in_1[5]);
  Multiplexer #(.width(6), .enable("false")) multiplexer_10 (
    .in0(multiplexer_5_out), .in1(multiplexer_9_out), .out(multiplexer_10_out), .sel(or_3_out));
  Multiplexer #(.width(6), .enable("false")) multiplexer_11 (
    .in0(multiplexer_10_out), .in1(multiplexer_1_out), .out(multiplexer_11_out), .sel(in_1[29]));
  not not_8 (not_8_out[5], not_2_out[5]);
  not not_9 (not_9_out, in_1[3]);
  or or_4 (or_4_out, not_9_out, in_1[2], in_1[1]);
  and and_4 (and_4_out, nor_1_out, or_4_out);
  xor xor_1 (xor_1_out, and_4_out, and_5_out);
  not not_10 (not_10_out, in_1[31]);
  and and_5 (and_5_out, in_1[29], not_10_out);
  Multiplexer #(.width(6), .enable("false")) multiplexer_12 (
    .in0({6{not_8_out[5]}}), .in1(multiplexer_11_out), .out(out_2), .sel(xor_1_out));

  // Notes on the sheet:
  //   Selecting Immediates
  //   Selecting Address
  //   Selecting A
  //   Selecting B
  //   1 if all 0
  //   Must be zero, no instruction has first two digits both 1
  //   ADDIU to XORI
  //   A (bits 20-16)
  //   B (bits 25-21)
  //   SLTI/SLTIU/LUI
  //   SA(immediate, bits 10-6)
  //   Address (bits 15-11)
  //   ADDU thru NOR
  //   Immediate (bits 15-0)
  //   SLL thru SRA
  //   Address (bits 20-16)
  //   A (bits 25-21)
  //   B (bits 20-16)
  //   SLLV thru SRAV
  //   MOVN/MOVZ
  //   Bits 29 and 5
  //   SLT/SLTU
endmodule

module MIPS32 (
);

  wire clock_1_out, equalandwrite_1_out_4, equalandwrite_2_out_4, equalandwrite_3_out_4,
       equalandwrite_4_out_4, execute_1_ctrlout, register_9_q, registerfile_1_p3;
  wire [4:0] decode_1_out_4, decode_1_out_5, decode_1_out_6, register_7_q, register_10_q, registerfile_1_p4;
  wire [5:0] decode_1_out_2, register_6_q;
  wire [31:0] decode_1_out_3, execute_1_d, mipsprogramrom_1_p1_2, mipsprogramrom_1_p2, multiplexer_1_out,
       multiplexer_2_out, multiplexer_3_out, multiplexer_4_out, register_1_q, register_3_q, register_4_q,
       register_5_q, register_8_q, registerfile_1_p1, registerfile_1_p7, registerfile_1_p8;
  wire [31:2] mipsprogramrom_1_p1;

  Clock clock_1 (.out(clock_1_out));
  // Incrementer #(.width(30)) incrementer_1: pin names not known
  Register #(.width(32)) register_1 (.D(mipsprogramrom_1_p2), .clk(clock_1_out), .Q(register_1_q));  // open: en, clr
  // MIPSProgramROM mipsprogramrom_1: pin names not known; wires that end beside it: {mipsprogramrom_1_p1, mipsprogramrom_1_p1_2[1:0]}, mipsprogramrom_1_p2
  Register #(.width(32)) register_2 (
    .D(mipsprogramrom_1_p1_2), .clk(clock_1_out), .Q({mipsprogramrom_1_p1, mipsprogramrom_1_p1_2[1:0]}));  // open: en, clr
  Decode decode_1 (
    .in_1(register_1_q), .out_2(decode_1_out_2), .out_3(decode_1_out_3), .out_4(decode_1_out_4),
    .out_5(decode_1_out_5), .out_6(decode_1_out_6));
  // RegisterFile #(.trigger("falling")) registerfile_1: pin names not known; wires that end beside it: registerfile_1_p1, clock_1_out, registerfile_1_p3, registerfile_1_p4, decode_1_out_5, decode_1_out_6, registerfile_1_p7, registerfile_1_p8
  equalandwrite equalandwrite_1 (
    .in_1(decode_1_out_5), .W(register_9_q), .in_3(register_10_q), .out_4(equalandwrite_1_out_4));
  equalandwrite equalandwrite_2 (
    .in_1(decode_1_out_6), .W(register_9_q), .in_3(register_10_q), .out_4(equalandwrite_2_out_4));
  Multiplexer #(.width(32), .enable("false")) multiplexer_1 (
    .in0(registerfile_1_p7), .in1(register_8_q), .out(multiplexer_1_out), .sel(equalandwrite_1_out_4));
  Multiplexer #(.width(32), .enable("false")) multiplexer_2 (
    .in0(registerfile_1_p8), .in1(register_8_q), .out(multiplexer_2_out), .sel(equalandwrite_2_out_4));
  Multiplexer #(.width(32), .enable("false")) multiplexer_3 (
    .in0(multiplexer_2_out), .in1(execute_1_d), .out(multiplexer_3_out), .sel(equalandwrite_4_out_4));
  equalandwrite equalandwrite_3 (
    .in_1(decode_1_out_5), .W(execute_1_ctrlout), .in_3(register_7_q), .out_4(equalandwrite_3_out_4));
  equalandwrite equalandwrite_4 (
    .in_1(decode_1_out_6), .W(execute_1_ctrlout), .in_3(register_7_q), .out_4(equalandwrite_4_out_4));
  Register #(.width(32)) register_3 (.D(multiplexer_4_out), .clk(clock_1_out), .Q(register_3_q));  // open: en, clr
  Multiplexer #(.width(32), .enable("false")) multiplexer_4 (
    .in0(multiplexer_1_out), .in1(execute_1_d), .out(multiplexer_4_out), .sel(equalandwrite_3_out_4));
  Register #(.width(32)) register_4 (.D(multiplexer_3_out), .clk(clock_1_out), .Q(register_4_q));  // open: en, clr
  Register #(.width(32)) register_5 (.D(decode_1_out_3), .clk(clock_1_out), .Q(register_5_q));  // open: en, clr
  Register #(.width(6)) register_6 (.D(decode_1_out_2), .clk(clock_1_out), .Q(register_6_q));  // open: en, clr
  Register #(.width(5)) register_7 (.D(decode_1_out_4), .clk(clock_1_out), .Q(register_7_q));  // open: en, clr
  Register #(.width(32)) register_8 (.D(execute_1_d), .clk(clock_1_out), .Q(register_8_q));  // open: en, clr
  Execute execute_1 (
    .A(register_3_q), .B(register_4_q), .Imm(register_5_q), .Ctrl(register_6_q), .D(execute_1_d),
    .CtrlOut(execute_1_ctrlout));
  Register #(.width(1)) register_9 (.D(execute_1_ctrlout), .clk(clock_1_out), .Q(register_9_q));  // open: en, clr
  Register #(.width(5)) register_10 (.D(register_7_q), .clk(clock_1_out), .Q(register_10_q));  // open: en, clr
  Register #(.width(32)) register_11 (.D(register_8_q), .clk(clock_1_out), .Q(registerfile_1_p1));  // open: en, clr
  Register #(.width(1)) register_12 (.D(register_9_q), .clk(clock_1_out), .Q(registerfile_1_p3));  // open: en, clr
  Register #(.width(5)) register_13 (.D(register_10_q), .clk(clock_1_out), .Q(registerfile_1_p4));  // open: en, clr

  // Notes on the sheet:
  //   contents of mipsprogramrom_1 (hex, n*v repeats v):
  //   ADDIU $t2, $zero, 4400 # testing addiu with positive immediate. result: t2 <- 4400 ADDU $t1, $t0,
  //   $t2 # testing addu. result: t1 <- 3900 SUBU $t1, $t0, $t2 # testing subu. result: t1 <- -4900 ANDI
  //   $t3, $t2, 8 # testing andi. result: t3 <- 0 ORI $t4, $t2, 6 # testing ori. result: t4 <- 2580 XORI
  //   $t5, $t2, 4 # testing xori. result: t5 <- 2584 SLTI $t6, $t2, -10 # testing slti with t2 > -10.
  //   result: t6 <- 0 SLTI $t6, $t2, 4402 # testing slti with t2 < 4402. result: t6 <- 1 SLTIU $t7, $t2, 3
  //   # testing slti with t2 > 3. result: t7 <- 0 SLTIU $t7, $t2, 4401 # testing slti with t2 < 4401.
  //   result: t7 <- 1  AND $t3, $t2, $t1 # testing and. result: t3 <- 10 OR $t4, $t3, $t1 # testing or.
  //   result: t4 <- 10 XOR $t5, $t4, $t3 # testing xor. result: t5 <- 0 NOR $t6, $t2, $t5 # testing nor.
  //   result: t6 <- -4401 SLT $t7, $t2, $t1 # testing slt with t2 > t1. result: t7 <- 0  SLT $t7, $t1, $t2
  //   # testing slt with t1 < t2. result: t7 <- 1 SLTU $t3, $t2, $t1 # testing sltu with t2 > t1. result:
  //   t3 <- 0 SLTU $t3, $t1, $t2 # testing sltu with t1 < t2. result: t3 <- 1 MOVN $t4, $t2, $t1 # testing
  //   movn with condition met. result: t4 <- t2. MOVN $t5, $t2, $zero # testing movn with condition not
  //   met. result: none MOVZ $t6, $t2, $t1 # testing movz with condition not met. result: none MOVZ $t7,
  //   $t2, $zero # testing movz with condition met. result: t7 <- t2 SLL $t3, $t2, 5 # testing sll.
  //   result: t3 <- 160 SRL $t4, $t2, 6 # testing srl. result: t4 <- 68 SRA $t5, $t2, 7 # testing sra.
  //   result: t5 <- 0 ADDIU $t3, $zero, 10 # result:  t3 <- 10 SLLV $t6, $t2, $t3 # testing sllv. result:
  //   t6 <- 10240 SRLV $t7, $t2, $t3 # testing srlv. result: t7 <- 4 SRAV $t3, $t2, $t3 # testing srav.
  //   result: t3 <- 44 loop: LUI $t4, 8019 # testing lui, creating loop for future tests. result: t4 <-
  //   4204265472 J loop # testing jump to loop. result: none JR $t5 # testing jr. result: none JAL loop #
  //   testing jal to loop. result: none JALR $t6 # testing jalr. result: none ADDIU $t4, $zero, 10 #
  //   result: t4 <- 10 BEQ $t6, $t7, 2424 # testing beq with condition not met. result: none BEQ $t3, $t4,
  //   2452 # testing beq with condition met. result: none BNE $t6, $t7, 4224 # testing bne with condition
  //   met. result: none BNE $t3, $t4, 2456 # testing bne with condition not met. result: none BLEZ $t6,
  //   2432 # testing blez with condition not met. result: none BLEZ $zero, 2436 # testing blez with
  //   condition met. result: none BGTZ $t6, 2440 # testing bgtz with condition met. result: none BGTZ
  //   $zero, 2428 # testing bgtz with condition not met. result: none BLTZ $t1, 2444 # testing bltz with
  //   condition met. result: none BLTZ $zero, 2448 # testing bltz with condition not met. result: none
  //   BGEZ $t6, 2448 # testing bgez. result: none LW $t6, 0($t7) # testing lw. result: none LB $t6,
  //   16($t7) #testing lb. result: none LBU $t6, 12($t7) # testing lbu. result: none SW $t6, 8($t7) #
  //   testing sw. result: none SB $t6, 4($t7) # testing sb. result: none
endmodule

module Execute (
  input  [31:0] A,
  input  [31:0] B,
  input  [31:0] Imm,
  input  [5:0] Ctrl,
  output [31:0] D,
  output CtrlOut
);

  wire and_1_out, and_2_out, and_3_out, and_4_out, and_5_out, comparator_1_lt, comparator_2_lt,
       multiplexer_2_out, nand_1_out, nand_2_out, nor_1_out, not_1_out, not_2_out, not_3_out, not_4_out,
       not_5_out, not_6_out, not_7_out, xor_1_out;
  wire [0:0] multiplexer_3_out;
  wire [31:0] mips_alu_1_p2, mips_alu_1_p5, multiplexer_1_out, multiplexer_4_out, multiplexer_6_out,
       multiplexer_7_out;

  Multiplexer #(.width(32), .enable("false")) multiplexer_1 (
    .in0(B), .in1(Imm), .out(multiplexer_1_out), .sel(Ctrl[4]));
  not not_1 (not_1_out, Ctrl[0]);
  not not_2 (not_2_out, Ctrl[1]);
  not not_3 (not_3_out, Ctrl[3]);
  not not_4 (not_4_out, Ctrl[1]);
  not not_5 (not_5_out, Ctrl[3]);
  Comparator #(.width(32)) comparator_1 (.a(A), .b(multiplexer_1_out), .lt(comparator_1_lt));  // open: gt, eq
  Comparator #(.width(32), .mode("unsigned")) comparator_2 (
    .a(A), .b(multiplexer_1_out), .lt(comparator_2_lt));  // open: gt, eq
  not not_6 (not_6_out, Ctrl[1]);
  and and_1 (and_1_out, Ctrl[0], not_6_out, not_7_out, Ctrl[3]);
  not not_7 (not_7_out, Ctrl[2]);
  and and_2 (and_2_out, Ctrl[3], Ctrl[5], Ctrl[4]);
  nand nand_1 (nand_1_out, Ctrl[0], Ctrl[1], Ctrl[2], Ctrl[3], Ctrl[4], Ctrl[5]);
  and and_3 (and_3_out, Ctrl[1], Ctrl[2], Ctrl[3]);
  and and_4 (and_4_out, not_1_out, not_2_out, Ctrl[2], not_3_out);
  and and_5 (and_5_out, Ctrl[0], not_4_out, Ctrl[2], not_5_out);
  Multiplexer #(.enable("false")) multiplexer_2 (
    .in0(comparator_1_lt), .in1(comparator_2_lt), .out(multiplexer_2_out), .sel(Ctrl[0]));
  nor nor_1 (nor_1_out, and_3_out, and_4_out, and_5_out);
  Multiplexer #(.enable("false")) multiplexer_3 (
    .in0(multiplexer_2_out), .in1(Ctrl[1]), .out(multiplexer_3_out[0]), .sel(Ctrl[3]));
  Multiplexer #(.width(32), .enable("false")) multiplexer_4 (
    .in0(multiplexer_1_out), .in1({{31{Ctrl[1]}}, multiplexer_3_out[0]}), .out(multiplexer_4_out),
    .sel(and_1_out));
  // Mips_ALU mips_alu_1: pin names not known; wires that end beside it: A, mips_alu_1_p2, Ctrl[3:0], multiplexer_1_out[4:0], mips_alu_1_p5
  Multiplexer #(.width(32), .enable("false")) multiplexer_5 (
    .in0(A), .in1(multiplexer_4_out), .out(mips_alu_1_p2), .sel(nor_1_out));
  Multiplexer #(.width(32), .enable("false")) multiplexer_6 (
    .in0(mips_alu_1_p5), .in1({{31{Ctrl[1]}}, multiplexer_3_out[0]}), .out(multiplexer_6_out), .sel(Ctrl[5]));
  Multiplexer #(.width(32), .enable("false")) multiplexer_7 (
    .in0(multiplexer_6_out), .in1({Imm[15:0], {16{Ctrl[1]}}}), .out(multiplexer_7_out), .sel(and_2_out));
  Multiplexer #(.width(32), .enable("false")) multiplexer_8 (
    .in0(multiplexer_7_out), .in1(B), .out(D), .sel(and_1_out));
  xor xor_1 (xor_1_out, mips_alu_1_p5[0], Ctrl[5]);
  nand nand_2 (nand_2_out, xor_1_out, and_1_out);
  and and_6 (CtrlOut, nand_2_out, nand_1_out);
endmodule

module equalandwrite (
  input  [4:0] in_1,
  input  W,
  input  [4:0] in_3,
  output out_4
);

  wire nor_1_out;
  wire [4:0] xor_1_out;

  assign xor_1_out = in_1 ^ in_3;  // XOR_Gate xor_1, 5 bits wide
  nor nor_1 (nor_1_out, xor_1_out[0], xor_1_out[1], xor_1_out[2], xor_1_out[3], xor_1_out[4]);
  and and_1 (out_4, nor_1_out, W);
endmodule
